# Fritzing sketch Ir5 (saved by Fritzing 0.9.3b)
circuit board: 6.38254cm x 3.94455cm
breadboards: 2

parts:
  R2 = Resistor [tolerance=±5% resistance=100 package=THT]
  R1 = Resistor [tolerance=±5% resistance=100 package=THT]
  Q2 = Basic FET N-Channel [package="TO220 [THT]"]
  R3 = Resistor [tolerance=±5% resistance=10k package=THT]
  R4 = Resistor [tolerance=±5% resistance=100 package=THT]
  R5 = Resistor [tolerance=±5% resistance=100 package=THT]
  IrR1 = OSRB38C9AA
  MCU1 = Raspberry Pi Zero
  LED1 = LED - 3mm [color="Infrared (940nm)" package="3 mm [THT]"]
  LED3 = LED - 3mm [color="Infrared (940nm)" package="3 mm [THT]"]
  LED4 = LED - 3mm [color="Infrared (940nm)" package="3 mm [THT]"]
  LED2 = LED - 3mm [color="Infrared (940nm)" package="3 mm [THT]"]
  LED5 = LED - 3mm [color="Red (633nm)" package="3 mm [THT]"]
  J5 = female pin header, 1 pin [form="♀ (female)"]
  J4 = female pin header, 6 pins [form="♀ (female)"]
  J6 = male pin header, 4 pins [form="♂ (male)"]
  Oled1 = OLED SSD1306

nets:
  N1: R2.Pin_0, R1.Pin_0, MCU1.pin_2, J5.pin1
  N2: R2.Pin_1, LED3.anode
  N3: R1.Pin_1, LED2.anode
  N4: Q2.gate, R3.Pin_0, R4.Pin_0, LED5.anode
  N5: Q2.drain, LED1.cathode, LED4.cathode
  GND: Q2.source, R3.Pin_1, R5.Pin_1, IrR1.GND, MCU1.pin_9, MCU1.pin_20, J4.pin5, J6.pin4, Oled1.GND
  N6: R4.Pin_1, MCU1.pin_7, J4.pin4
  N7: R5.Pin_0, LED5.cathode
  N8: IrR1.OUT, MCU1.pin_11, J4.pin6
  VCC: IrR1.VCC, MCU1.pin_1, J4.pin1, J6.pin3, Oled1.VCC
  N9: MCU1.pin_3, J4.pin2, J6.pin1, Oled1.SDA
  N10: MCU1.pin_5, J4.pin3, J6.pin2, Oled1.SCL
  N11: LED1.anode, LED2.cathode
  N12: LED3.cathode, LED4.anode

custom parts:
  OSRB38C9AA: 7..4*6..2*5..25mm Infrared Receiiver Modulle
  OLED SSD1306: OLED powered by a SSD1306 driver over I2C interface.
